# Fritzing sketch carone-v4 (saved by Fritzing 0.9.2b)
circuit board: 6.31939cm x 4.80069cm
breadboards: 1

parts:
  74HCT4052N = IC, DIP package, 16 pins [chip_label=74HCT4052N]
  Arduino = Arduino Pro Mini v13
  Q2 = NPN-Transistor [package="TO92 [THT]"]
  DTR = Header 1 [package=1x01_offset]
  TX = Header 1 [package=1x01_offset]
  RX = Header 1 [package=1x01_offset]
  5v = Header 1 [package=1x01_offset]
  GND = Header 1 [package=1x01_offset]
  5v->3v3 = Voltage Regulator LM1117 [package=sot223]
  SDA = Header 1 [package=1x01_offset]
  SCL = Header 1 [package=1x01_offset]
  L-Gyro-Tx = Header 1 [package=1x01_offset]
  R-Gyro-Tx = Header 1 [package=1x01_offset]
  R-Gyro-Rx = Header 1 [package=1x01_offset]
  L-Gyro-Rx = Header 1 [package=1x01_offset]
  Q3 = NPN-Transistor [package="TO92 [THT]"]
  L-Hall-Y = Header 1 [package=1x01_offset]
  R-Hall-Y = Header 1 [package=1x01_offset]
  L-Hall-B = Header 1 [package=1x01_offset]
  R-Hall-B = Header 1 [package=1x01_offset]
  R14v_In = Header 1 [package=1x01_offset]
  L14v_In = Header 1 [package=1x01_offset]
  L14v_Out = Header 1 [package=1x01_offset]
  R14v_Out = Header 1 [package=1x01_offset]
  GND_2 = Header 1 [package=1x01_offset]
  GND_3 = Header 1 [package=1x01_offset]
  GND_4 = Header 1 [package=1x01_offset]
  GND_5 = Header 1 [package=1x01_offset]
  14v = Header 1 [package=1x01_offset]
  5v_2 = Header 1 [package=1x01_offset]
  GND_6 = Header 1 [package=1x01_offset]
  GND_7 = Header 1 [package=1x01_offset]
  R2 = Resistor [tolerance=±5% resistance=1k package=THT]
  D2 = Diode [package=diode-1n4001]
  D1 = Diode [package=diode-1n4001]
  D3 = Diode [package=diode-1n4001]
  D4 = Diode [package=diode-1n4001]
  R4 = Resistor [tolerance=±5% resistance=1k package=THT]
  R3 = Resistor [tolerance=±5% resistance=10k package=THT]
  R1 = Resistor [tolerance=±5% resistance=1k package=THT]
  R5 = Resistor [tolerance=±5% resistance=1k package=THT]
  C1 = Electrolytic Capacitor [capacitance=10nF voltage=20V package="100 mil [THT, electrolytic]"]

nets:
  N1: 74HCT4052N.pin1, Q2.C, R2.Pin_1
  N2: 74HCT4052N.pin3, R-Gyro-Tx.1
  N3: 74HCT4052N.pin5, R-Gyro-Rx.1
  N4: 74HCT4052N.pin6, 74HCT4052N.pin8, 74HCT4052N.pin9, Arduino.GND, Q2.E, GND.1, 5v->3v3.ADJ, Q3.E, GND_2.1, GND_3.1, GND_4.1, GND_5.1, GND_6.1, GND_7.1, C1.-
  N5: 74HCT4052N.pin10, Arduino.D7, R3.Pin_1
  N6: 74HCT4052N.pin12, Q3.C, R1.Pin_1
  N7: 74HCT4052N.pin13, L-Gyro-Tx.1
  N8: 74HCT4052N.pin14, L-Gyro-Rx.1
  N9: 74HCT4052N.pin16, Arduino.VCC, 5v.1, 5v->3v3.IN, 5v_2.1, R3.Pin_0
  N10: Arduino.DTR, DTR.1
  N11: Arduino.D0/TX, TX.1
  N12: Arduino.D1/RX, RX.1
  N13: Arduino.A4, SDA.1
  N14: Arduino.A5, SCL.1
  N15: Arduino.D9_PWM, R4.Pin_0
  N16: Arduino.D8, R5.Pin_0
  N17: Arduino.D5_PWM, R-Hall-B.1
  N18: Arduino.D4, L-Hall-B.1
  N19: Arduino.D3_PWM, R-Hall-Y.1
  N20: Arduino.D2, L-Hall-Y.1
  N21: Q2.B, R4.Pin_1
  N22: 5v->3v3.OUT, R2.Pin_0, R1.Pin_0, C1.+
  N23: Q3.B, R5.Pin_1
  N24: R14v_In.1, D1.A
  N25: L14v_In.1, D2.A
  N26: L14v_Out.1, D2.C, D4.A
  N27: R14v_Out.1, D1.C, D3.A
  N28: 14v.1, D3.C, D4.C

notes:
  DC-DC Step Down
  |
  -
  CarOne Schema
