# Fritzing sketch data-selector-v3 (saved by Fritzing 0.9.2b)
circuit board: 6cm x 4cm
breadboards: 1

parts:
  R_G_IN = NPN-Transistor [package="TO92 [THT]"]
  R_A_IN = NPN-Transistor [package="TO92 [THT]"]
  R_OUT = NPN-Transistor [package="TO92 [THT]"]
  L_Rx = Header 1 [package=1x01_offset]
  R_Rx = Header 1 [package=1x01_offset]
  GND = Header 1 [package=1x01_offset]
  Swi = Header 1 [package=1x01_offset]
  5v = Header 1 [package=1x01_offset]
  14vIN = Header 1 [package=1x01_offset]
  GND_2 = Header 1 [package=1x01_offset]
  C->G = Header 1 [package=1x01_offset]
  L_Tx = Header 1 [package=1x01_offset]
  G<-C = Header 1 [package=1x01_offset]
  14vOUT = Header 1 [package=1x01_offset]
  GND_3 = Header 1 [package=1x01_offset]
  L_G_Rx = Header 1 [package=1x01_offset]
  R_G_Rx = Header 1 [package=1x01_offset]
  14vOUT_2 = Header 1 [package=1x01_offset]
  G<-C_2 = Header 1 [package=1x01_offset]
  R_Tx = Header 1 [package=1x01_offset]
  14vIN_2 = Header 1 [package=1x01_offset]
  GND_4 = Header 1 [package=1x01_offset]
  GND_5 = Header 1 [package=1x01_offset]
  C->G_2 = Header 1 [package=1x01_offset]
  14v_DC/DC_Step_Down = Header 1 [package=1x01_offset]
  5v_OUT = Header 1 [package=1x01_offset]
  GND_6 = Header 1 [package=1x01_offset]
  GND_7 = Header 1 [package=1x01_offset]
  Sw_1k = Resistor [tolerance=±5% resistance=1k package=THT]
  Sw_P_D = Resistor [tolerance=±5% resistance=10k package=THT]
  L_Sw = NPN-Transistor [package="TO92 [THT]"]
  L_G_IN = NPN-Transistor [package="TO92 [THT]"]
  L_OUT = NPN-Transistor [package="TO92 [THT]"]
  L_A_IN = NPN-Transistor [package="TO92 [THT]"]
  5v->3v3 = Voltage Regulator LM1117 [package=sot223]
  R9 = Resistor [tolerance=±5% resistance=1k package=THT]
  R10 = Resistor [tolerance=±5% resistance=1k package=THT]
  R_3v3_D_IN1 = Resistor [tolerance=±5% resistance=1k package=THT]
  R11 = Resistor [tolerance=±5% resistance=1k package=THT]
  R_3v3_D_P_UP1 = Resistor [tolerance=±5% resistance=10k package=THT]
  L_3v3_D_IN = Resistor [tolerance=±5% resistance=1k package=THT]
  R_5v_D_P_DOWN1 = Resistor [tolerance=±5% resistance=10k package=THT]
  R_5v_D_IN = Resistor [tolerance=±5% resistance=1k package=THT]
  R_5v_D_P_DOWN2 = Resistor [tolerance=±5% resistance=10k package=THT]
  L_5v_D_IN = Resistor [tolerance=±5% resistance=1k package=THT]
  R_3v3_D_P_UP2 = Resistor [tolerance=±5% resistance=10k package=THT]
  R13 = Resistor [tolerance=±5% resistance=1k package=THT]
  R14 = Resistor [tolerance=±5% resistance=1k package=THT]
  R12 = Resistor [tolerance=±5% resistance=1k package=THT]
  R_Sw = NPN-Transistor [package="TO92 [THT]"]

nets:
  GND: R_G_IN.E, R_A_IN.E, R_OUT.E, GND.1, GND_2.1, GND_3.1, GND_4.1, GND_5.1, GND_6.1, GND_7.1, Sw_P_D.Pin_1, L_Sw.E, L_G_IN.E, L_OUT.E, L_A_IN.E, 5v->3v3.ADJ, R_5v_D_P_DOWN1.Pin_1, R_5v_D_P_DOWN2.Pin_1, R_Sw.E
  N1: R_G_IN.B, R_3v3_D_IN1.Pin_1, R_Sw.C
  N2: R_G_IN.C, R_A_IN.C, R9.Pin_0, R11.Pin_0
  N3: R_A_IN.B, R_5v_D_IN.Pin_1
  N4: R_OUT.B, R9.Pin_1
  R 3.3v Data OUT (PullUp): R_OUT.C, R_Tx.1, R10.Pin_1
  L 5.0v Data IN: L_Rx.1, R_Rx.1, R_5v_D_P_DOWN1.Pin_0, R_5v_D_IN.Pin_0, R_5v_D_P_DOWN2.Pin_0, L_5v_D_IN.Pin_0
  Switch 5.0v: Swi.1, Sw_1k.Pin_0, Sw_P_D.Pin_0
  N5: 5v.1, 5v_OUT.1, 5v->3v3.IN
  N6: 14vIN.1, 14vOUT.1, 14vOUT_2.1, 14vIN_2.1, 14v_DC/DC_Step_Down.1
  N7: C->G.1, G<-C.1
  L 3.3v Data OUT (PullUp): L_Tx.1, L_OUT.C, R12.Pin_1
  L 3.3v Data IN: L_G_Rx.1, L_3v3_D_IN.Pin_0, R_3v3_D_P_UP2.Pin_0
  R 3.3v Data IN: R_G_Rx.1, R_3v3_D_IN1.Pin_0, R_3v3_D_P_UP1.Pin_0
  N8: G<-C_2.1, C->G_2.1
  N9: Sw_1k.Pin_1, L_Sw.B, R_Sw.B
  N10: L_Sw.C, L_G_IN.B, L_3v3_D_IN.Pin_1
  N11: L_G_IN.C, L_A_IN.C, R13.Pin_0, R14.Pin_0
  N12: L_OUT.B, R13.Pin_1
  N13: L_A_IN.B, L_5v_D_IN.Pin_1
  3.3V: 5v->3v3.OUT, R10.Pin_0, R11.Pin_1, R_3v3_D_P_UP1.Pin_1, R_3v3_D_P_UP2.Pin_1, R14.Pin_1, R12.Pin_0
